# Fritzing sketch Circuit_diagrams (saved by Fritzing 1.0.1rc)
breadboards: 1

parts:
  R1 = Resistor [tolerance=±5% power=0.25W resistance=220 package=THT]
  VCC1 = Battery block 9V
  R2 = Resistor [tolerance=±5% power=0.25W resistance=220 package=THT]

nets:
  N1: R1.Pin_0, VCC1.-, R2.Pin_0
  N2: R1.Pin_1, VCC1.+, R2.Pin_1
