# Fritzing sketch SSD1306 (saved by Fritzing 1.0.1rc)

parts:
  Onderdeel1 = Arduino Uno (Rev3) - ICSP
  OLED_I2C1 = OLED 128x64 I2C Monochrome Display

nets:
  N1: Onderdeel1.A4/SDA, OLED_I2C1.SDA
  N2: Onderdeel1.A5/SCL, OLED_I2C1.SCK
  5V: Onderdeel1.5V, OLED_I2C1.VDD
  GND: Onderdeel1.GND, OLED_I2C1.GND
