# Fritzing sketch BME280 (saved by Fritzing 0.9.10b)
breadboards: 1

parts:
  Onderdeel1 = Arduino Uno (Rev3) - ICSP
  Onderdeel2 = GY-BMEP280 Barometric Pressure Sensor - Breakout

nets:
  GND: Onderdeel1.GND, Onderdeel2.GND
  N1: Onderdeel1.D10_PWM/SS, Onderdeel2.CSB
  N2: Onderdeel1.D11_PWM/MOSI, Onderdeel2.SDA
  N3: Onderdeel1.D12/MISO, Onderdeel2.SDO
  N4: Onderdeel1.D13/SCK, Onderdeel2.SCL
  3V3: Onderdeel1.3V3, Onderdeel2.VCC

notes:
  Vcc 3V3 GND SCK SDI CSB SDO <-SPI
  SCL SDA <-IIC

custom parts:
  GY-BMEP280 Barometric Pressure Sensor - Breakout: The BME280 is a chip which was originally designed for the next generation of smartphones. It is made up of a very accurate pressure sensor and an associated temperature sensor which helps calibrate the pressure readings. And just for fun they threw in a pretty solid humidity sensor in there as well! So with an I2C connection you have access to enough weather data to make some pretty good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
