# Fritzing sketch BMP280 (saved by Fritzing 1.0.1rc)
breadboards: 1

parts:
  Onderdeel1 = Arduino Uno (Rev3) - ICSP
  Onderdeel2 = GY-BMEP280 Barometric Pressure Sensor - Breakout
  Q3 = MOSFET-NCHANNEL [package=sot323]
  Q4 = MOSFET-NCHANNEL [package=sot323]
  R1 = Resistor [tolerance=±5% resistance=10k package="2010 [SMD]"]
  R2 = Resistor [tolerance=±5% resistance=10k package="2010 [SMD]"]
  Q5 = MOSFET-NCHANNEL [package=sot323]
  Q6 = MOSFET-NCHANNEL [package=sot323]
  R3 = Resistor [tolerance=±5% resistance=10k package="2010 [SMD]"]
  R4 = Resistor [tolerance=±5% resistance=10k package="2010 [SMD]"]

nets:
  N1: Onderdeel1.ICSP_MOSI, Onderdeel1.D11_PWM/MOSI, Q3.D, R1.Pin_1
  N2: Onderdeel1.D10_PWM/SS, Q5.D, R3.Pin_1
  N3: Onderdeel1.D12/MISO, Q6.D, R4.Pin_1
  N4: Onderdeel1.D13/SCK, Q4.D, R2.Pin_1
  GND: Onderdeel1.GND, Onderdeel2.GND
  3V3: Onderdeel1.3V3, Onderdeel2.VCC, Q3.G, Q4.G, Q5.G, Q6.G
  N5: Onderdeel1.5V, R1.Pin_0, R2.Pin_0, R4.Pin_0
  N6: Onderdeel2.SCL, Q4.S
  N7: Onderdeel2.SDA, Q3.S
  N8: Onderdeel2.CSB, Q5.S
  N9: Onderdeel2.SDO, Q6.S

notes:
  Vcc 3V3 GND SCK SDI CSB SDO <-SPI
  SCL SDA <-IIC
  5V
  3V3

custom parts:
  GY-BMEP280 Barometric Pressure Sensor - Breakout: The BME280 is a chip which was originally designed for the next generation of smartphones. It is made up of a very accurate pressure sensor and an associated temperature sensor which helps calibrate the pressure readings. And just for fun they threw in a pretty solid humidity sensor in there as well! So with an I2C connection you have access to enough weather data to make some pretty good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
