# Fritzing sketch GYML8511 (saved by Fritzing 1.0.1rc)
breadboards: 1

parts:
  PART1 = ML8511 UV Sensor Breakout [part_number=SEN-12705]  # not connected
  Onderdeel1 = Arduino Uno (Rev3) - ICSP

nets:
  N1: Onderdeel1.A1, Onderdeel1.3V3

custom parts:
  ML8511 UV Sensor Breakout: Description: The ML8511 breakout is an easy to use ultraviolet light sensor. The MP8511 UV Sensor works by outputing an analog signal in relation to the amount of UV light it detects. This breakout can be very handy in creating devices that warn the user of sunburn or detect the UV index as it relates to weather conditions. This sensor breakout can detect 280-390nm light most effectively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
