# Fritzing sketch LDR-NTC (saved by Fritzing 0.9.10b)
breadboards: 1

parts:
  Onderdeel1 = Arduino Uno (Rev3) - ICSP
  R1 = Photocell (LDR) [package=THT]
  R2 = Resistor [tolerance=±5% power=0.25 resistance=10k package=THT]

nets:
  N1: Onderdeel1.A0, R1.pin_1, R2.Pin_0
  N2: Onderdeel1.5V, R1.pin_0
  N3: Onderdeel1.GND, R2.Pin_1
