# Fritzing sketch LDR-R-measuring (saved by Fritzing 0.9.10b)
breadboards: 1

parts:
  R1 = Photocell (LDR) [package=THT]
  V1 = DC Power [voltage=5]
  VM1 = Multimeter (DC Voltage)
  R2 = Resistor [tolerance=±5% power=0.25 resistance=10k package=THT]

nets:
  N1: R1.pin_0, V1.V+
  N2: R1.pin_1, VM1.V_Probe, R2.Pin_0
  N3: V1.V-, VM1.COM_Probe, R2.Pin_1

notes:
  +5V    GND
