# Fritzing sketch PWM (saved by Fritzing 1.0.1rc)
breadboards: 1

parts:
  F1 = Fan - Ventilador [package=THT]
  D1 = Rectifier Diode [part_number=1N4001 package="Melf DO-213 AB [SMD]"]
  Onderdeel2 = Arduino Uno (Rev3)

nets:
  N1: F1.5V, D1.anode
  GND: F1.GND, Onderdeel2.GND
  N2: D1.cathode, Onderdeel2.VIN

notes:
  12V

custom parts:
  Fan - Ventilador: Ventilador de 2 pines, se encuentra comunmente en computadoras de escritorio
