# Fritzing sketch LED-Button (saved by Fritzing 0.9.10b)
breadboards: 1

parts:
  UNO = Arduino Uno (Rev3) - ICSP
  R3 = Resistor [tolerance=±5% power=0.25 resistance=1k package=THT]
  S1 = SWITCH-MOMENTARY-2 [package=tactile-pth-12mm]
  LED1 = smd LED [color="Red (633nm)" package="0805 [SMD]"]

nets:
  N1: UNO.5V, R3.Pin_0
  N2: UNO.D2, LED1.cathode
  N3: UNO.D3_PWM, S1.1
  N4: UNO.GND, S1.2
  N5: R3.Pin_1, LED1.anode
