# Fritzing sketch Arduino_DS18B20_probe (saved by Fritzing 1.0.1rc)
breadboards: 1

parts:
  DS2 = DS18B20 1-Wire Temperature Sensor Probe  # not connected
  Onderdeel1 = Arduino Uno (Rev3)
  R1 = Resistor [tolerance=±5% resistance=1k package="0805 [SMD]"]

nets:
  N1: Onderdeel1.D12/MISO, R1.Pin_0
  N2: Onderdeel1.5V, R1.Pin_1
