# Fritzing sketch L298N (saved by Fritzing 1.0.1rc)

parts:
  Onderdeel1 = Arduino Uno (Rev3) - ICSP
  M1 = linear actuator Actuonix-l12 [package=THT]
  L298N1 = L298N DC motor driver

nets:
  N1: Onderdeel1.D3_PWM, L298N1.ENB
  N2: Onderdeel1.D4, L298N1.IN4
  N3: Onderdeel1.D5_PWM, L298N1.IN3
  5V: Onderdeel1.5V, L298N1.5V
  N4: M1.pin2, L298N1.OUT3
  N5: M1.pin3, L298N1.OUT4

notes:
  12V

custom parts:
  linear actuator Actuonix-l12: Actuonix-l12 linear actuator.
  L298N DC motor driver: 2x DC motor driver with 78M05 positive voltage regulator (7..35 V) L298N: max 46 V, 2 A Set 5 V Enable jumper to enable 5 V regultor (needed for the L298N) and +5 V output at screw terminal or supply external +5 V at screw terminal Set ENA and/or ENB to +5 V to enable motor permanently or supply ENA and/or ENB with PWM signal IN1 and IN2 set rotation directory for motor A (OUT1/OUT2) IN2 and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
