# Fritzing sketch HC595 (saved by Fritzing 1.0.1rc)
breadboards: 1

parts:
  R1 = Resistor [tolerance=±5% power=0.25W resistance=470 package=THT]
  R2 = Resistor [tolerance=±5% power=0.25W resistance=470 package=THT]
  R3 = Resistor [tolerance=±5% power=0.25W resistance=470 package=THT]
  R4 = Resistor [tolerance=±5% power=0.25W resistance=470 package=THT]
  R5 = Resistor [tolerance=±5% power=0.25W resistance=470 package=THT]
  R6 = Resistor [tolerance=±5% power=0.25W resistance=470 package=THT]
  R7 = Resistor [tolerance=±5% power=0.25W resistance=470 package=THT]
  R8 = Resistor [tolerance=±5% power=0.25W resistance=470 package=THT]
  LED3 = smd LED [color="Red (633nm)" package="0805 [SMD]"]
  LED4 = smd LED [color="Red (633nm)" package="0805 [SMD]"]
  LED5 = smd LED [color="Red (633nm)" package="0805 [SMD]"]
  LED6 = smd LED [color="Red (633nm)" package="0805 [SMD]"]
  LED7 = smd LED [color="Red (633nm)" package="0805 [SMD]"]
  LED8 = smd LED [color="Red (633nm)" package="0805 [SMD]"]
  LED9 = smd LED [color="Red (633nm)" package="0805 [SMD]"]
  LED10 = smd LED [color="Red (633nm)" package="0805 [SMD]"]
  U1 = 74HC595 [package="DIP16 [THT]"]
  Onderdeel1 = Arduino Uno (Rev3) - ICSP

nets:
  N1: R1.Pin_0, LED9.anode
  N2: R1.Pin_1, U1.Q1
  N3: R2.Pin_0, LED8.anode
  N4: R2.Pin_1, U1.Q2
  N5: R3.Pin_0, LED7.anode
  N6: R3.Pin_1, U1.Q3
  N7: R4.Pin_0, LED10.anode
  N8: R4.Pin_1, U1.Q0
  N9: R5.Pin_0, LED6.anode
  N10: R5.Pin_1, U1.Q4
  N11: R6.Pin_0, LED5.anode
  N12: R6.Pin_1, U1.Q5
  N13: R7.Pin_0, LED4.anode
  N14: R7.Pin_1, U1.Q6
  N15: R8.Pin_0, LED3.anode
  N16: R8.Pin_1, U1.Q7
  GND: LED3.cathode, LED4.cathode, LED5.cathode, LED6.cathode, LED7.cathode, LED8.cathode, LED9.cathode, LED10.cathode, U1.GND, U1.OE, Onderdeel1.GND
  VCC: U1.MR, U1.VCC, Onderdeel1.5V
  N17: U1.SH_CP, Onderdeel1.D12/MISO
  N18: U1.ST_CP, Onderdeel1.D8
  N19: U1.DS, Onderdeel1.ICSP_MOSI, Onderdeel1.D11_PWM/MOSI
