# Fritzing sketch linear-actuator (saved by Fritzing 1.0.1rc)

parts:
  Onderdeel1 = Arduino Uno (Rev3) - ICSP
  U1 = 4-Channel 5v Relay Shield [package=relay-4ch5v10a]
  M1 = linear actuator Actuonix-l12 [package=THT]

nets:
  N1: Onderdeel1.D6_PWM, U1.IN2
  N2: Onderdeel1.D7, U1.IN1
  5V: Onderdeel1.5V, U1.VCC
  GND: Onderdeel1.GND, U1.GND
  N3: U1.K1-In, U1.K2-In
  N4: U1.K1-Off, M1.pin3
  N5: U1.K1-On, U1.K2-On
  N6: U1.K2-Off, M1.pin2

notes:
  12V
  - NO (normally open)
  - COM (common connection)
  - NC (normally closed)

custom parts:
  4-Channel 5v Relay Shield: 4 Channel 5v Relay Shield w. 2x SPD-06VDC-SD-C
  linear actuator Actuonix-l12: Actuonix-l12 linear actuator.
