# Fritzing sketch LM538 (saved by Fritzing 1.0.1rc)
breadboards: 1

parts:
  Onderdeel1 = Arduino Uno (Rev3)
  U1 = LM 358 Dual Op-Amp [package="DIP8 [THT]"]
  R1 = Photocell (LDR) [power=0.25W dark_resistance_@0.01lx=300kΩ light_resistance_@100lx=400Ω luminance=10lx package=THT]
  R2 = Resistor [tolerance=±5% resistance=10k package="2512 [SMD]"]
  R3 = 12mm Trimmer Potentiometer (Large) [maximum_resistance=10kΩ knob_status=50% power=0.5W package=THT]

nets:
  N1: Onderdeel1.D7, U1.connector0
  N2: Onderdeel1.5V, U1.connector7, R1.pin_0, R3.leg1
  N3: Onderdeel1.GND, U1.connector3, R2.Pin_1, R3.leg2
  N4: U1.connector1, U1.connector4, R3.wiper
  N5: U1.connector2, U1.connector5, R1.pin_1, R2.Pin_0
